# Fritzing sketch OfficeRoomSinricLCD_REMOTE (saved by Fritzing 0.9.3b)
breadboards: 1

parts:
  Part2 = LCD1602-I2C
  InfraRedsensor = TSOP312.., 314.. [package=THT]
  R3 = Resistor [tolerance=±5% resistance=1k package="0402 [SMD]"]
  C3 = Electrolytic Capacitor [capacitance=4.7µF voltage=63V package="200 mil [THT, electrolytic]"]
  U2 = NodeMCU V3.0
  U3 = 4-Channel 5v Relay Shield [package=relay-4ch5v10a]

nets:
  GND: Part2.GND, InfraRedsensor.GND, C3.-, U2.GND#6, U2.GND#13, U2.GND#16, U2.GND#33, U3.GND
  VCC: Part2.VCC, U2.Vin, U3.VCC
  N1: Part2.SDA, U2.D2
  N2: Part2.SCL, U2.D1
  N3: InfraRedsensor.Vs, R3.Pin_0, C3.+
  N4: InfraRedsensor.Data, U2.D7
  N5: R3.Pin_1, U2.3V3
  N6: U2.D3, U3.IN1
  N7: U2.D4, U3.IN2
  N8: U2.D5, U3.IN3
  N9: U2.D6, U3.IN4

custom parts:
  LCD1602-I2C: A standard character display, usually with 2x16 characters. Comes in many colors with LCM1602 IIC attached.
  NodeMCU V3.0: ESP8266 based NodeMCU
  4-Channel 5v Relay Shield: 4 Channel 5v Relay Shield w. 2x SPD-06VDC-SD-C
